# Fritzing sketch прототип 2 (saved by Fritzing 0.9.3b)
breadboards: 1

parts:
  S1 = Pushbutton [package="[THT]"]
  S4 = Pushbutton [package="[THT]"]
  LED1 = LED - 5mm [color="Green (570nm)" package="5 mm [THT]"]
  LED2 = LED - 5mm [color="Yellow (595nm)" package="5 mm [THT]"]
  LED3 = LED - 5mm [color="Orange (620nm)" package="5 mm [THT]"]
  LED4 = LED - 5mm [color="Red (633nm)" package="5 mm [THT]"]
  Часть1 = Arduino Uno (Rev3)
  S2 = Pushbutton [package="[THT]"]
  S5 = Pushbutton [package="[THT]"]
  VCC1 = Battery
  S6 = Toggle Switch [package=THT]
  R1 = Resistor [tolerance=±5% resistance=220 package=THT]
  J1 = Piezo Speaker
  Q1 = NPN-Transistor [package="TO92 [THT]"]

nets:
  N1: S1.Pin_1, S1.Pin_2, Часть1.D4
  N2: S1.Pin_3, S1.Pin_4, S4.Pin_3, S4.Pin_4, Часть1.GND, S2.Pin_3, S2.Pin_4, S5.Pin_1, S5.Pin_2, S6.L2, R1.Pin_1, J1.pin1, Q1.E
  N3: S4.Pin_1, S4.Pin_2, Часть1.D3_PWM
  N4: LED1.cathode, Часть1.D10_PWM/SS
  N5: LED1.anode, LED2.anode, LED3.anode, LED4.anode, R1.Pin_0
  N6: LED2.cathode, Часть1.D9_PWM
  N7: LED3.cathode, Часть1.D8
  N8: LED4.cathode, Часть1.D7
  N9: Часть1.D11_PWM/MOSI, Q1.B
  N10: Часть1.D2, S2.Pin_1, S2.Pin_2
  N11: Часть1.D5_PWM, S5.Pin_3, S5.Pin_4
  N12: Часть1.D6_PWM, S6.COM
  N13: Часть1.VIN, VCC1.-, VCC1.+, J1.pin2, Q1.C
